# Fritzing sketch electronic_diagram (saved by Fritzing 0.8.7b)
breadboards: 1

parts:
  Arduino_Mega = Arduino Mega 2560 (Rev3)
  LCD1 = LCD screen
  P1 = POT [package=pot_alpha_rv16af-20]
  R1 = Resistor [tolerance=±5% resistance=220 package=THT]
  Keypad4x4 = Keypad Membran 4x4
  S1 = SPST Switch [package=switch-spst-smd-a]
  LED1 = RGB LED (com. cathode, rbg) [package="5 mm [THT]"]
  74xx1 = 74xx08 Logic AND Gate [part_number=74HC08 package="DIP (Dual Inline) [THT]"]
  R4 = Resistor [tolerance=±5% resistance=220 package=THT]
  LED2 = LED - 5mm [color="Red (633nm)" package="5 mm [THT]"]
  7-segments_U1 = 7-SEGMENT-DISPLAY [package=7-segment-display]
  CD4511 = CD4511
  CD4511_2 = CD4511
  7-segments_U2 = 7-SEGMENT-DISPLAY [package=7-segment-display]
  R5 = Resistor [tolerance=±5% resistance=220 package=THT]
  LED3 = LED - 5mm [color="Red (633nm)" package="5 mm [THT]"]

nets:
  GND: Arduino_Mega.GND, LCD1.VSS, LCD1.LED-, P1.A, LED1.common_cathode, LED2.cathode, 7-segments_U1.G1, 7-segments_U1.DP, 7-segments_U1.G2, CD4511.GND, CD4511_2.GND, 7-segments_U2.G1, 7-segments_U2.DP, 7-segments_U2.G2, LED3.cathode
  N1: Arduino_Mega.D13_PWM, LCD1.RS
  N2: Arduino_Mega.D12_PWM, LCD1.E
  N3: Arduino_Mega.D11_PWM, LCD1.DB4
  N4: Arduino_Mega.D10_PWM, LCD1.DB5
  N5: Arduino_Mega.D9_PWM, LCD1.DB6
  N6: Arduino_Mega.D8_PWM, LCD1.DB7
  VCC: Arduino_Mega.5V, LCD1.VDD, P1.E, R1.Pin_1, CD4511.VCC, CD4511_2.VCC
  N7: Arduino_Mega.D7_PWM, S1.S, LED1.blue_anode
  N8: Arduino_Mega.D22, Keypad4x4.Pin1
  N9: Arduino_Mega.D23, Keypad4x4.Pin2
  N10: Arduino_Mega.D24, Keypad4x4.Pin3
  N11: Arduino_Mega.D25, Keypad4x4.Pin4
  N12: Arduino_Mega.D26, Keypad4x4.Pin5
  N13: Arduino_Mega.D27, Keypad4x4.Pin6
  N14: Arduino_Mega.D28, Keypad4x4.Pin7
  N15: Arduino_Mega.D29, Keypad4x4.Pin8
  N16: Arduino_Mega.D30, 74xx1.1A
  N17: Arduino_Mega.D31, 74xx1.1B
  N18: Arduino_Mega.D35, 74xx1.1Y, R4.Pin_1
  N19: Arduino_Mega.D37, R5.Pin_0
  N20: Arduino_Mega.D38, CD4511.INPUT_1
  N21: Arduino_Mega.D39, CD4511.INPUT_4
  N22: Arduino_Mega.D40, CD4511.LE
  N23: Arduino_Mega.D41, CD4511.BL
  N24: Arduino_Mega.D42, CD4511.LT
  N25: Arduino_Mega.D43, CD4511.INPUT_3
  N26: Arduino_Mega.D44, CD4511.INPUT_2
  N27: Arduino_Mega.D46, CD4511_2.INPUT_1
  N28: Arduino_Mega.D47, CD4511_2.INPUT_4
  N29: Arduino_Mega.D48, CD4511_2.LE
  N30: Arduino_Mega.D49, CD4511_2.BL
  N31: Arduino_Mega.D50, CD4511_2.LT
  N32: Arduino_Mega.D51, CD4511_2.INPUT_3
  N33: Arduino_Mega.D52, CD4511_2.INPUT_2
  N34: LCD1.V0, P1.S
  N35: LCD1.LED+, R1.Pin_0, S1.P
  N36: S1.O, LED1.red_anode
  N37: R4.Pin_0, LED2.anode
  N38: 7-segments_U1.E, CD4511.OUTPUT_E
  N39: 7-segments_U1.D, CD4511.OUTPUT_D
  N40: 7-segments_U1.C, CD4511.OUTPUT_C
  N41: 7-segments_U1.B, CD4511.OUTPUT_B
  N42: 7-segments_U1.A, CD4511.OUTPUT_A
  N43: 7-segments_U1.F, CD4511.OUTPUT_F
  N44: 7-segments_U1.G, CD4511.OUTPUT_G
  N45: CD4511_2.OUTPUT_E, 7-segments_U2.E
  N46: CD4511_2.OUTPUT_D, 7-segments_U2.D
  N47: CD4511_2.OUTPUT_C, 7-segments_U2.C
  N48: CD4511_2.OUTPUT_B, 7-segments_U2.B
  N49: CD4511_2.OUTPUT_A, 7-segments_U2.A
  N50: CD4511_2.OUTPUT_G, 7-segments_U2.G
  N51: CD4511_2.OUTPUT_F, 7-segments_U2.F
  N52: R5.Pin_1, LED3.anode

custom parts:
  Keypad Membran 4x4: Membrane Keypad 4x4 Matrix
  74xx08 Logic AND Gate: IC containing quadruple 2-input positive-AND gates.
  CD4511: CD4511 j'ai dit
